// Logisim project CPU.circ as structural Verilog: 2 circuits, main circuit main
module main (
);

  Reg32 reg32_1 ();  // open: RegWrite, WriteReg, WriteData, ReadReg1, ReadReg2, Reset, ReadData1, ReadData2
endmodule

module Reg32 (
  input  RegWrite,
  input  [4:0] WriteReg,
  input  [31:0] WriteData,
  input  [4:0] ReadReg1,
  input  [4:0] ReadReg2,
  input  Reset,
  output [31:0] ReadData1,
  output [31:0] ReadData2
);

  wire CLK, W0, W1, W2, W3, W4, W5, W6, W7;
  wire [31:0] R0, R1, R2, R3, R4, R5, R6, R7;

  Register #(.width(32)) register_1 (.D(WriteData), .en(W0), .clk(CLK), .Q(R0), .clr(Reset));
  Register #(.width(32)) register_2 (.D(WriteData), .en(W4), .clk(CLK), .Q(R4), .clr(Reset));
  Register #(.width(32)) register_3 (.D(WriteData), .en(W1), .clk(CLK), .Q(R1), .clr(Reset));
  Register #(.width(32)) register_4 (.D(WriteData), .en(W1), .clk(CLK), .Q(R1), .clr(Reset));
  Register #(.width(32)) register_5 (.D(WriteData), .en(W1), .clk(CLK), .Q(R1), .clr(Reset));
  Register #(.width(32)) register_6 (.D(WriteData), .en(W1), .clk(CLK), .Q(R1), .clr(Reset));
  Register #(.width(32)) register_7 (.D(WriteData), .en(W1), .clk(CLK), .Q(R1), .clr(Reset));
  Register #(.width(32)) register_8 (.D(WriteData), .en(W1), .clk(CLK), .Q(R1), .clr(Reset));
  Register #(.width(32)) register_9 (.D(WriteData), .en(W1), .clk(CLK), .Q(R1), .clr(Reset));
  Register #(.width(32)) register_10 (.D(WriteData), .en(W5), .clk(CLK), .Q(R5), .clr(Reset));
  Register #(.width(32)) register_11 (.D(WriteData), .en(W1), .clk(CLK), .Q(R1), .clr(Reset));
  Register #(.width(32)) register_12 (.D(WriteData), .en(W1), .clk(CLK), .Q(R1), .clr(Reset));
  Register #(.width(32)) register_13 (.D(WriteData), .en(W1), .clk(CLK), .Q(R1), .clr(Reset));
  Register #(.width(32)) register_14 (.D(WriteData), .en(W1), .clk(CLK), .Q(R1), .clr(Reset));
  Register #(.width(32)) register_15 (.D(WriteData), .en(W1), .clk(CLK), .Q(R1), .clr(Reset));
  Register #(.width(32)) register_16 (.D(WriteData), .en(W1), .clk(CLK), .Q(R1), .clr(Reset));
  Register #(.width(32)) register_17 (.D(WriteData), .en(W2), .clk(CLK), .Q(R2), .clr(Reset));
  Register #(.width(32)) register_18 (.D(WriteData), .en(W6), .clk(CLK), .Q(R6), .clr(Reset));
  Register #(.width(32)) register_19 (.D(WriteData), .en(W1), .clk(CLK), .Q(R1), .clr(Reset));
  Register #(.width(32)) register_20 (.D(WriteData), .en(W1), .clk(CLK), .Q(R1), .clr(Reset));
  Register #(.width(32)) register_21 (.D(WriteData), .en(W1), .clk(CLK), .Q(R1), .clr(Reset));
  Register #(.width(32)) register_22 (.D(WriteData), .en(W1), .clk(CLK), .Q(R1), .clr(Reset));
  Register #(.width(32)) register_23 (.D(WriteData), .en(W1), .clk(CLK), .Q(R1), .clr(Reset));
  Register #(.width(32)) register_24 (.D(WriteData), .en(W1), .clk(CLK), .Q(R1), .clr(Reset));
  Register #(.width(32)) register_25 (.D(WriteData), .en(W3), .clk(CLK), .Q(R3), .clr(Reset));
  Register #(.width(32)) register_26 (.D(WriteData), .en(W7), .clk(CLK), .Q(R7), .clr(Reset));
  Register #(.width(32)) register_27 (.D(WriteData), .en(W1), .clk(CLK), .Q(R1), .clr(Reset));
  Register #(.width(32)) register_28 (.D(WriteData), .en(W1), .clk(CLK), .Q(R1), .clr(Reset));
  Register #(.width(32)) register_29 (.D(WriteData), .en(W1), .clk(CLK), .Q(R1), .clr(Reset));
  Register #(.width(32)) register_30 (.D(WriteData), .en(W1), .clk(CLK), .Q(R1), .clr(Reset));
  Register #(.width(32)) register_31 (.D(WriteData), .en(W1), .clk(CLK), .Q(R1), .clr(Reset));
  Register #(.width(32)) register_32 (.D(WriteData), .en(W1), .clk(CLK), .Q(R1), .clr(Reset));
  Clock clock_1 (.out(CLK));
  Multiplexer #(.select(5), .width(32)) multiplexer_1 (
    .in0(R0), .in1(R1), .in2(R2), .in3(R3), .in4(R4), .in5(R5), .in6(R6), .in7(R7), .out(ReadData1),
    .sel(ReadReg1));  // open: in8, in9, in10, in11, in12, in13, in14, in15, in16, in17, in18, in19, in20, in21, in22, in23, in24, in25, in26, in27, in28, in29, in30, in31
  Multiplexer #(.select(5), .width(32)) multiplexer_2 (
    .in0(R0), .in1(R1), .in2(R2), .in3(R3), .in4(R4), .in5(R5), .in6(R6), .in7(R7), .out(ReadData2),
    .sel(ReadReg2));  // open: in8, in9, in10, in11, in12, in13, in14, in15, in16, in17, in18, in19, in20, in21, in22, in23, in24, in25, in26, in27, in28, in29, in30, in31
  Decoder #(.select(5)) decoder_1 (
    .out0(W0), .out1(W1), .out2(W2), .out3(W3), .out4(W4), .out5(W5), .out6(W6), .out7(W7), .sel(WriteReg),
    .en(RegWrite));  // open: out8, out9, out10, out11, out12, out13, out14, out15, out16, out17, out18, out19, out20, out21, out22, out23, out24, out25, out26, out27, out28, out29, out30, out31

  // Other names for the same wires on the sheet: R = Reset; WD[31:0] = WriteData
endmodule
